// Logisim project Examen.circ as structural Verilog: 1 circuit, main circuit main
module main (
  input  in_1,
  input  in_2,
  input  in_3,
  input  in_4,
  input  in_5,
  input  in_6
);

  wire CLK, comparator_1_eq, comparator_1_gt, comparator_2_eq, comparator_2_gt, Contar_L, Contar_V,
       not_3_out, not_4_out, or_1_out, or_2_out, Pausa;
  wire [6:0] adder_1_out, adder_2_out, adder_3_out, Local, not_1_out, not_2_out, Puntos_a_sumar,
       register_2_q, Visitante;

  assign not_1_out = ~Visitante;  // NOT_Gate not_1, 7 bits wide
  assign not_2_out = ~Local;  // NOT_Gate not_2, 7 bits wide
  not not_3 (not_3_out, Pausa);
  not not_4 (not_4_out, Pausa);
  Clock clock_1 (.out(CLK));
  // Probe on adder_1_out
  Adder #(.width(7)) adder_1 (.a(Local), .b(not_1_out), .out(adder_1_out), .cin(1'b1));  // open: cout
  // Probe on adder_2_out
  Adder #(.width(7)) adder_2 (.a(Visitante), .b(not_2_out), .out(adder_2_out), .cin(1'b1));  // open: cout
  and and_1 (Contar_V, not_3_out, in_3);
  and and_2 (Contar_L, not_4_out, in_1);
  Comparator #(.width(7)) comparator_1 (
    .a(adder_1_out), .b(7'b0110010), .gt(comparator_1_gt), .eq(comparator_1_eq));  // open: lt
  Comparator #(.width(7), .mode("unsigned")) comparator_2 (
    .a(adder_2_out), .b(7'b0110010), .gt(comparator_2_gt), .eq(comparator_2_eq));  // open: lt
  or or_1 (or_1_out, comparator_1_gt, comparator_1_eq);
  or or_2 (or_2_out, comparator_2_gt, comparator_2_eq);
  or or_3 (Pausa, or_1_out, or_2_out);
  Register #(.width(7)) register_1 (.D(adder_3_out), .en(Contar_L), .Q(Local), .clk(CLK), .clr(in_4));
  Register #(.width(7)) register_2 (.D(Visitante), .en(Contar_V), .Q(register_2_q), .clk(CLK), .clr(in_4));
  Multiplexer #(.select(3), .width(7), .disabled(0), .enable("false")) multiplexer_1 (
    .in0({7{1'b0}}), .in1(7'b0000001), .in2(7'b0000010), .in4(7'b0000011), .out(Puntos_a_sumar),
    .sel({in_6, in_5, in_2}));  // open: in3, in5, in6, in7
  Adder #(.width(7)) adder_3 (.a(Local), .b(Puntos_a_sumar), .out(adder_3_out));  // open: cin, cout
  Adder #(.width(7)) adder_4 (.a(register_2_q), .b(Puntos_a_sumar), .out(Visitante));  // open: cin, cout

  // Other names for the same wires on the sheet: P1 = in_2; P2 = in_5; P3 = in_6; INICIO = in_4; L = in_1; V = in_3
endmodule
