// Logisim project T203.circ as structural Verilog: 1 circuit, main circuit main
module main (
  input  [3:0] A,
  input  [3:0] B,
  input  [3:0] C
);

  wire A___B___C_t, A___B_t, A___C_t, B___A___C, B___C_t, C___A___B, C___B___A, not_1_out, not_2_out,
       not_3_out, not_4_out;
  wire [3:0] A___B, A___B___C, A___C, B___C, not_5_out, Y;

  Comparator #(.width(4), .mode("unsigned")) comparator_1 (.a(A), .b(B), .gt(A___B_t));  // open: eq, lt
  Comparator #(.width(4), .mode("unsigned")) comparator_2 (.a(A), .b(C), .gt(A___C_t));  // open: eq, lt
  Comparator #(.width(4), .mode("unsigned")) comparator_3 (.a(B), .b(C), .gt(B___C_t));  // open: eq, lt
  and and_1 (A___B___C_t, A___B_t, A___C_t);
  and and_2 (C___A___B, A___B_t, not_1_out);
  not not_1 (not_1_out, A___C_t);
  not not_2 (not_2_out, A___B_t);
  and and_3 (B___A___C, not_2_out, A___C_t);
  not not_3 (not_3_out, A___B_t);
  and and_4 (C___B___A, not_3_out, not_4_out);
  not not_4 (not_4_out, A___C_t);
  // Probe on A___C
  Adder #(.width(4)) adder_1 (.a(A), .b(C), .out(A___C));  // open: cin, cout
  Adder #(.width(4)) adder_2 (.a(A___C), .b(not_5_out), .out(A___B___C), .cin(1'b1));  // open: cout
  assign not_5_out = ~B;  // NOT_Gate not_5, 4 bits wide
  // Probe on A___B___C
  Multiplexer #(.select(4), .width(4), .disabled(0), .enable("false")) multiplexer_1 (
    .in1(A___B), .in2(A___C), .in4(B___C), .in8(A___B___C), .out(Y),
    .sel({C___B___A, B___A___C, C___A___B, A___B___C_t}));  // open: in0, in3, in5, in6, in7, in9, in10, in11, in12, in13, in14, in15
  // Probe on A___B
  Adder #(.width(4)) adder_3 (.a(A), .b(B), .out(A___B));  // open: cin, cout
  Adder #(.width(4)) adder_4 (.a(B), .b(C), .out(B___C));  // open: cin, cout
  // Probe on Y
  // Probe on B___C
endmodule
