// Logisim project test.circ as structural Verilog: 1 circuit, main circuit main
module main (
  input  [3:0] A,
  input  [3:0] B,
  input  [3:0] C
);

  wire A___B_t, A___C_t, B___C_t;
  wire [3:0] A___B, A___B___C, A___C, B___C, not_1_out, undriven, Y;

  Comparator #(.width(4), .mode("unsigned")) comparator_1 (.a(A), .b(B), .gt(A___B_t));  // open: eq, lt
  Comparator #(.width(4), .mode("unsigned")) comparator_2 (.a(A), .b(C), .gt(A___C_t));  // open: eq, lt
  Comparator #(.width(4), .mode("unsigned")) comparator_3 (.a(B), .b(C), .gt(B___C_t));  // open: eq, lt
  // Probe on B___C
  Adder #(.width(4)) adder_1 (.a(B), .b(C), .out(B___C));  // open: cin, cout
  Adder #(.width(4)) adder_2 (.a(A), .b(C), .out(A___C));  // open: cin, cout
  // Probe on A___C
  Adder #(.width(4)) adder_3 (.a(A___C), .b(not_1_out), .out(A___B___C), .cin(1'b1));  // open: cout
  assign not_1_out = ~A;  // NOT_Gate not_1, 4 bits wide
  // Probe on A___B___C
  Adder #(.width(4)) adder_4 (.a(A), .b(B), .out(A___B));  // open: cin, cout
  // Probe on A___B
  Multiplexer #(.select(4), .width(4), .disabled(0), .enable("false")) multiplexer_1 (
    .in2(A___B), .in4(B___C), .in8(A___B___C), .in9(A___B___C), .out(Y), .sel(undriven));  // open: in0, in1, in3, in5, in6, in7, in10, in11, in12, in13, in14, in15
  // Probe on Y
endmodule
